// Logisim project mips-like.circ as structural Verilog: 14 circuits, main circuit PROCESSADOR
module PROCESSADOR (
  output [31:0] \INSTRUÇÃO 
);

  wire and_1_out, button_1_out, clock_1_out, ex_mem_1_out_14, ex_mem_1_out_15, ex_mem_1_out_16,
       ex_mem_1_out_17, ex_mem_1_out_18, ex_mem_1_out_19, id_ex_1_branch_2, id_ex_1_data_hazard_2,
       id_ex_1_memread_2, id_ex_1_memto_reg, id_ex_1_memwrite_2, id_ex_1_regdst, id_ex_1_regwrite_2,
       id_ex_1_ula_src_2, mem_wb_1_memtoreg_2, mem_wb_1_regwrite_2, UC_branch, UC_data_hazard, UC_memread,
       UC_memtoreg, UC_memwrite, UC_regdst, UC_regwrite, UC_ula_op0, UC_ula_op1, UC_ula_src, ula_1_branch;
  wire [1:0] id_ex_1_ula_op0_2;
  wire [3:0] ex_mem_1_out_22, id_ex_1_out_33, id_ex_1_out_34, mem_wb_1_out_12, multiplexer_4_out;
  wire [19:0] ula_to_mem_1_saida;
  wire [31:0] adder_1_out, adder_2_out, banco_de_registradores_1_r0_d, banco_de_registradores_1_r1_d,
       bit_extender_1_out, ex_mem_1_out_13, ex_mem_1_out_20, ex_mem_1_out_21, id_ex_1_out_20, id_ex_1_out_30,
       id_ex_1_out_31, id_ex_1_out_32, if_id_1_out_5, mem_wb_1_out_10, mem_wb_1_out_11, multiplexer_1_out,
       multiplexer_2_out, multiplexer_3_out, multiplexer_5_out, PC_q, ram_1_data, rom_1_data, shifter_1_out,
       ula_1_ula_out;

  Multiplexer #(.width(32), .enable("false")) multiplexer_1 (
    .in0(adder_1_out), .in1(ex_mem_1_out_13), .out(multiplexer_1_out), .sel(and_1_out));
  Register #(.width(32)) PC (.D(multiplexer_1_out), .Q(PC_q), .clk(clock_1_out), .clr(button_1_out));  // open: en
  Clock clock_1 (.out(clock_1_out));
  Adder #(.width(32)) adder_1 (.a(32'h4), .b(PC_q), .out(adder_1_out));  // open: cin, cout
  Button button_1 (.out(button_1_out));
  IF___ID if_id_1 (
    .add_4(adder_1_out), .pc(rom_1_data), .CLK(clock_1_out), .Clear(button_1_out), .out_5(if_id_1_out_5),
    .out_6(\INSTRUÇÃO ));
  ROM #(.addrWidth(24), .dataWidth(32)) rom_1 (.addr(PC_q[25:2]), .data(rom_1_data));  // open: sel
  UC UC (
    .E3(\INSTRUÇÃO [31]), .E2(\INSTRUÇÃO [30]), .E1(\INSTRUÇÃO [29]), .E0(\INSTRUÇÃO [28]),
    .RegDst(UC_regdst), .data_hazard(UC_data_hazard), .branch(UC_branch), .MemRead(UC_memread),
    .MemToReg(UC_memtoreg), .ula_op0(UC_ula_op0), .ula_op1(UC_ula_op1), .MemWrite(UC_memwrite),
    .ula_src(UC_ula_src), .RegWrite(UC_regwrite));
  BANCO_DE_REGISTRADORES banco_de_registradores_1 (
    .DATA_WRITE(multiplexer_5_out), .CLK(clock_1_out), .RW(mem_wb_1_out_12),
    .R0_D(banco_de_registradores_1_r0_d), .R0(\INSTRUÇÃO [27:24]), .R1_D(banco_de_registradores_1_r1_d),
    .R1(\INSTRUÇÃO [23:20]), .RW_2(mem_wb_1_regwrite_2), .RESET(button_1_out));
  assign bit_extender_1_out = {{16{\INSTRUÇÃO [15]}}, \INSTRUÇÃO [15:0]};  // Bit_Extender bit_extender_1
  ID___EX id_ex_1 (
    .regwrite(UC_regwrite), .branch(UC_branch), .MemRead(UC_memread), .MeToReg(UC_memtoreg),
    .ula_op0(UC_ula_op0), .ula_op1(UC_ula_op1), .MemWrite(UC_memwrite), .ula_src(UC_ula_src),
    .reg0(banco_de_registradores_1_r0_d), .data_write(bit_extender_1_out), .in_15(\INSTRUÇÃO [23:20]),
    .CLK(clock_1_out), .Clear(button_1_out), .regwrite_2(id_ex_1_regwrite_2), .branch_2(id_ex_1_branch_2),
    .MemRead_2(id_ex_1_memread_2), .MemTo_Reg(id_ex_1_memto_reg), .ula_op0_2(id_ex_1_ula_op0_2[0]),
    .ula_op1_2(id_ex_1_ula_op0_2[1]), .MemWrite_2(id_ex_1_memwrite_2), .ula_src_2(id_ex_1_ula_src_2),
    .out_30(id_ex_1_out_30), .out_31(id_ex_1_out_31), .out_32(id_ex_1_out_32), .out_33(id_ex_1_out_33),
    .reg1(banco_de_registradores_1_r1_d), .in_2(if_id_1_out_5), .out_20(id_ex_1_out_20), .ResDst(UC_regdst),
    .RegDst(id_ex_1_regdst), .in_16(\INSTRUÇÃO [19:16]), .out_34(id_ex_1_out_34),
    .data_hazard(UC_data_hazard), .data_hazard_2(id_ex_1_data_hazard_2));
  Multiplexer #(.width(32), .enable("false")) multiplexer_2 (
    .in0(id_ex_1_out_30), .in1(ex_mem_1_out_21), .out(multiplexer_2_out), .sel(id_ex_1_data_hazard_2));
  Multiplexer #(.width(32), .enable("false")) multiplexer_3 (
    .in0(id_ex_1_out_31), .in1(id_ex_1_out_32), .out(multiplexer_3_out), .sel(id_ex_1_ula_src_2));
  Shifter #(.width(32)) shifter_1 (.in(id_ex_1_out_32), .\dist (5'b00010), .out(shifter_1_out));
  ULA ula_1 (
    .DATA_0(multiplexer_2_out), .DATA_1(multiplexer_3_out), .ULA_OUT(ula_1_ula_out),
    .ULA_OP(id_ex_1_ula_op0_2), .branch(ula_1_branch));
  Multiplexer #(.width(4), .enable("false")) multiplexer_4 (
    .in0(id_ex_1_out_33), .in1(id_ex_1_out_34), .out(multiplexer_4_out), .sel(id_ex_1_regdst));
  Adder #(.width(32)) adder_2 (.a(id_ex_1_out_20), .b(shifter_1_out), .out(adder_2_out));  // open: cin, cout
  EX___MEM ex_mem_1 (
    .in_2(id_ex_1_regwrite_2), .in_3(id_ex_1_branch_2), .in_4(ula_1_branch), .in_5(id_ex_1_memread_2),
    .in_6(id_ex_1_memwrite_2), .in_8(id_ex_1_out_31), .in_9(ula_1_ula_out), .in_10(multiplexer_4_out),
    .CLK(clock_1_out), .CLEAR(button_1_out), .out_14(ex_mem_1_out_14), .out_15(ex_mem_1_out_15),
    .out_16(ex_mem_1_out_16), .out_17(ex_mem_1_out_17), .out_18(ex_mem_1_out_18), .out_20(ex_mem_1_out_20),
    .out_21(ex_mem_1_out_21), .out_22(ex_mem_1_out_22), .in_7(id_ex_1_memto_reg), .out_19(ex_mem_1_out_19),
    .in_1(adder_2_out), .out_13(ex_mem_1_out_13));
  ula_to_mem ula_to_mem_1 (.entrada(ex_mem_1_out_21), .saida(ula_to_mem_1_saida));
  and and_1 (and_1_out, ex_mem_1_out_15, ex_mem_1_out_16);
  RAM #(.addrWidth(20), .dataWidth(32), .bus("separate")) ram_1 (
    .addr(ula_to_mem_1_saida), .din(ex_mem_1_out_20), .data(ram_1_data), .str(ex_mem_1_out_18),
    .clk(clock_1_out), .ld(ex_mem_1_out_17), .clr(button_1_out));  // open: sel
  MEM___WB mem_wb_1 (
    .MemToReg(ex_mem_1_out_19), .in_3(ram_1_data), .in_4(ex_mem_1_out_21), ._24_27(ex_mem_1_out_22),
    .CLK(clock_1_out), .CLEAR(button_1_out), .MemToReg_2(mem_wb_1_memtoreg_2), .out_10(mem_wb_1_out_10),
    .out_11(mem_wb_1_out_11), .out_12(mem_wb_1_out_12), .RegWrite(ex_mem_1_out_14),
    .RegWrite_2(mem_wb_1_regwrite_2));
  Multiplexer #(.width(32), .enable("false")) multiplexer_5 (
    .in0(mem_wb_1_out_11), .in1(mem_wb_1_out_10), .out(multiplexer_5_out), .sel(mem_wb_1_memtoreg_2));

  // Notes on the sheet:
  //   contents of rom_1 (hex, n*v repeats v):
  //   32020010 4*0 3c0c0020 4*0 34040001 4*0 3f0f0004 4*0 87f00071 4*0 70600000 4*0 86f00060 4*0 70e00000
  //   4*0 8ef00036 4*0 1f790000 e9e90000 4*0 19490000 e9100000 4*0 40000000 4*0 1ef90000 e9690000 4*0
  //   19490000 e9230000 4*0 43300000 4*0 10390000 e9550000 4*0 3e0e0001 4*0 8aafffcd 4*0 1f790000 e9690000
  //   4*0 19490000 e9cb0000 4*0 5b500000 4*0 70500000 4*0 36060001 4*0 8aafffa3 4*0 37070001 4*0 8aafff8f
  //   BANCO DE REGISTRADORES
  //   ULA
endmodule

module ULA (
  input  [31:0] DATA_0,
  input  [31:0] DATA_1,
  input  [1:0] ULA_OP,
  output branch,
  output [31:0] ULA_OUT
);

  wire comparator_1_eq, comparator_1_gt;
  wire [31:0] adder_1_out, multiplier_1_out, shifter_1_out;

  Adder #(.width(32)) adder_1 (.a(DATA_0), .b(DATA_1), .out(adder_1_out));  // open: cin, cout
  Multiplier #(.width(32)) multiplier_1 (.a(DATA_0), .b(DATA_1), .out(multiplier_1_out));  // open: cin, cout
  Comparator #(.width(32), .mode("unsigned")) comparator_1 (
    .a(DATA_0), .b(DATA_1), .gt(comparator_1_gt), .eq(comparator_1_eq));  // open: lt
  Shifter #(.width(32)) shifter_1 (.in(DATA_0), .\dist (DATA_1[4:0]), .out(shifter_1_out));
  or or_1 (branch, comparator_1_gt, comparator_1_eq);
  Multiplexer #(.select(2), .width(32), .enable("false")) multiplexer_1 (
    .in0(adder_1_out), .in1(multiplier_1_out), .in2(DATA_1), .in3(shifter_1_out), .out(ULA_OUT), .sel(ULA_OP));
endmodule

module UC (
  input  E3,
  input  E2,
  input  E1,
  input  E0,
  output RegDst,
  output data_hazard,
  output branch,
  output MemRead,
  output MemToReg,
  output ula_op0,
  output ula_op1,
  output MemWrite,
  output ula_src,
  output RegWrite
);

  wire and_1_out, and_2_out, and_3_out, and_4_out, and_5_out, and_8_out, and_9_out, and_10_out, and_11_out,
       and_12_out, and_13_out, and_14_out, and_15_out, and_17_out, and_18_out, and_19_out, and_20_out,
       and_21_out, and_22_out, and_23_out, and_24_out, not_1_out, not_2_out, not_3_out, not_4_out, not_5_out,
       not_6_out, not_7_out, not_8_out, not_9_out, not_10_out, not_11_out, not_12_out, not_13_out,
       not_14_out, not_15_out, not_16_out, not_17_out, not_18_out, not_19_out, not_20_out, not_21_out,
       not_22_out, not_23_out, not_24_out, not_25_out, not_26_out, not_27_out, not_28_out, not_29_out,
       not_30_out, not_31_out, not_32_out, not_33_out, not_34_out, not_35_out, not_36_out;

  not not_1 (not_1_out, E3);
  and and_1 (and_1_out, not_1_out, not_2_out, E0);
  not not_2 (not_2_out, E2);
  not not_3 (not_3_out, E3);
  and and_2 (and_2_out, not_3_out, not_4_out, E1);
  not not_4 (not_4_out, E2);
  and and_3 (and_3_out, E3, E2, E1);
  not not_5 (not_5_out, E0);
  and and_4 (and_4_out, E3, not_6_out, not_7_out);
  not not_6 (not_6_out, E2);
  not not_7 (not_7_out, E0);
  and and_5 (and_5_out, E3, E2, not_8_out);
  not not_8 (not_8_out, E1);
  and and_6 (MemRead, E2, not_9_out, not_10_out);
  not not_9 (not_9_out, E1);
  not not_10 (not_10_out, E0);
  not not_11 (not_11_out, E1);
  and and_7 (MemToReg, E2, not_11_out, not_12_out);
  not not_12 (not_12_out, E0);
  not not_13 (not_13_out, E3);
  not not_14 (not_14_out, E2);
  not not_15 (not_15_out, E1);
  not not_16 (not_16_out, E2);
  not not_17 (not_17_out, E0);
  not not_18 (not_18_out, E1);
  not not_19 (not_19_out, E0);
  not not_20 (not_20_out, E2);
  not not_21 (not_21_out, E0);
  not not_22 (not_22_out, E3);
  not not_23 (not_23_out, E1);
  not not_24 (not_24_out, E0);
  not not_25 (not_25_out, E3);
  not not_26 (not_26_out, E1);
  not not_27 (not_27_out, E2);
  not not_28 (not_28_out, E0);
  not not_29 (not_29_out, E3);
  and and_8 (and_8_out, not_29_out, not_30_out, E1);
  not not_30 (not_30_out, E2);
  not not_31 (not_31_out, E2);
  and and_9 (and_9_out, not_31_out, E1, E0);
  and and_10 (and_10_out, E2, not_32_out);
  not not_32 (not_32_out, E1);
  not not_33 (not_33_out, E3);
  and and_11 (and_11_out, not_33_out, E2, E0);
  not not_34 (not_34_out, E3);
  and and_12 (and_12_out, not_34_out, E0);
  not not_35 (not_35_out, E3);
  and and_13 (and_13_out, not_35_out, E1);
  not not_36 (not_36_out, E3);
  and and_14 (and_14_out, not_36_out, E2);
  and and_15 (and_15_out, E2, E1);
  or or_1 (RegDst, and_1_out, and_2_out, and_3_out);
  and and_16 (data_hazard, E3, E2, E1, not_5_out);
  or or_2 (branch, and_4_out, and_5_out);
  and and_17 (and_17_out, not_13_out, not_14_out, not_15_out, E0);
  and and_18 (and_18_out, not_16_out, E1, not_17_out);
  or or_3 (ula_op0, and_17_out, and_18_out, and_19_out);
  and and_19 (and_19_out, E3, E2, not_18_out, not_19_out);
  and and_20 (and_20_out, not_20_out, E1, not_21_out);
  or or_4 (ula_op1, and_20_out, and_21_out, and_22_out);
  and and_21 (and_21_out, not_22_out, E2, E1);
  and and_22 (and_22_out, E3, E2, not_23_out, not_24_out);
  and and_23 (and_23_out, not_25_out, E2, not_26_out, E0);
  or or_5 (MemWrite, and_23_out, and_24_out);
  and and_24 (and_24_out, E3, not_27_out, E1, not_28_out);
  or or_6 (ula_src, and_8_out, and_9_out, and_10_out, and_11_out);
  or or_7 (RegWrite, and_12_out, and_13_out, and_14_out, and_15_out);
endmodule

module BANCO_DE_REGISTRADORES (
  input  [31:0] DATA_WRITE,
  input  [3:0] R0,
  input  [3:0] R1,
  input  CLK,
  input  [3:0] RW,
  input  RESET,
  input  RW_2,
  output [31:0] R0_D,
  output [31:0] R1_D
);

  wire demultiplexer_1_out0, demultiplexer_1_out1, demultiplexer_1_out2, demultiplexer_1_out3,
       demultiplexer_1_out4, demultiplexer_1_out5, demultiplexer_1_out6, demultiplexer_1_out7,
       demultiplexer_1_out8, demultiplexer_1_out9, demultiplexer_1_out10, demultiplexer_1_out11,
       demultiplexer_1_out12, demultiplexer_1_out13, demultiplexer_1_out14, demultiplexer_1_out15;
  wire [31:0] register_1_q, register_2_q, register_3_q, register_4_q, register_5_q, register_6_q,
       register_7_q, register_8_q, register_9_q, register_10_q, register_11_q, register_12_q, register_13_q,
       register_14_q, register_15_q, register_16_q;

  Demultiplexer #(.select(4), .enable("false")) demultiplexer_1 (
    .out0(demultiplexer_1_out0), .out1(demultiplexer_1_out1), .out2(demultiplexer_1_out2),
    .out3(demultiplexer_1_out3), .out4(demultiplexer_1_out4), .out5(demultiplexer_1_out5),
    .out6(demultiplexer_1_out6), .out7(demultiplexer_1_out7), .out8(demultiplexer_1_out8),
    .out9(demultiplexer_1_out9), .out10(demultiplexer_1_out10), .out11(demultiplexer_1_out11),
    .out12(demultiplexer_1_out12), .out13(demultiplexer_1_out13), .out14(demultiplexer_1_out14),
    .out15(demultiplexer_1_out15), .in(RW_2), .sel(RW));
  Register #(.width(32)) register_1 (
    .D(DATA_WRITE), .en(demultiplexer_1_out0), .Q(register_1_q), .clk(CLK), .clr(RESET));
  Register #(.width(32)) register_2 (
    .D(DATA_WRITE), .en(demultiplexer_1_out1), .Q(register_2_q), .clk(CLK), .clr(RESET));
  Register #(.width(32)) register_3 (
    .D(DATA_WRITE), .en(demultiplexer_1_out2), .Q(register_3_q), .clk(CLK), .clr(RESET));
  Register #(.width(32)) register_4 (
    .D(DATA_WRITE), .en(demultiplexer_1_out3), .Q(register_4_q), .clk(CLK), .clr(RESET));
  Register #(.width(32)) register_5 (
    .D(DATA_WRITE), .en(demultiplexer_1_out4), .Q(register_5_q), .clk(CLK), .clr(RESET));
  Register #(.width(32)) register_6 (
    .D(DATA_WRITE), .en(demultiplexer_1_out5), .Q(register_6_q), .clk(CLK), .clr(RESET));
  Register #(.width(32)) register_7 (
    .D(DATA_WRITE), .en(demultiplexer_1_out6), .Q(register_7_q), .clk(CLK), .clr(RESET));
  Register #(.width(32)) register_8 (
    .D(DATA_WRITE), .en(demultiplexer_1_out7), .Q(register_8_q), .clk(CLK), .clr(RESET));
  Register #(.width(32)) register_9 (
    .D(DATA_WRITE), .en(demultiplexer_1_out8), .Q(register_9_q), .clk(CLK), .clr(RESET));
  Register #(.width(32)) register_10 (
    .D(DATA_WRITE), .en(demultiplexer_1_out9), .Q(register_10_q), .clk(CLK), .clr(RESET));
  Register #(.width(32)) register_11 (
    .D(DATA_WRITE), .en(demultiplexer_1_out10), .Q(register_11_q), .clk(CLK), .clr(RESET));
  Register #(.width(32)) register_12 (
    .D(DATA_WRITE), .en(demultiplexer_1_out11), .Q(register_12_q), .clk(CLK), .clr(RESET));
  Register #(.width(32)) register_13 (
    .D(DATA_WRITE), .en(demultiplexer_1_out12), .Q(register_13_q), .clk(CLK), .clr(RESET));
  Register #(.width(32)) register_14 (
    .D(DATA_WRITE), .en(demultiplexer_1_out13), .Q(register_14_q), .clk(CLK), .clr(RESET));
  Register #(.width(32)) register_15 (
    .D(DATA_WRITE), .en(demultiplexer_1_out14), .Q(register_15_q), .clk(CLK), .clr(RESET));
  Register #(.width(32)) register_16 (
    .D(DATA_WRITE), .en(demultiplexer_1_out15), .Q(register_16_q), .clk(CLK), .clr(RESET));
  Multiplexer #(.select(4), .width(32), .disabled(0), .enable("false")) multiplexer_1 (
    .in0(register_1_q), .in1(register_2_q), .in2(register_3_q), .in3(register_4_q), .in4(register_5_q),
    .in5(register_6_q), .in6(register_7_q), .in7(register_8_q), .in8(register_9_q), .in9(register_10_q),
    .in10(register_11_q), .in11(register_12_q), .in12(register_13_q), .in13(register_14_q),
    .in14(register_15_q), .in15(register_16_q), .out(R0_D), .sel(R0));
  Multiplexer #(.select(4), .width(32), .enable("false")) multiplexer_2 (
    .in0(register_1_q), .in1(register_2_q), .in2(register_3_q), .in3(register_4_q), .in4(register_5_q),
    .in5(register_6_q), .in6(register_7_q), .in7(register_8_q), .in8(register_9_q), .in9(register_10_q),
    .in10(register_11_q), .in11(register_12_q), .in12(register_13_q), .in13(register_14_q),
    .in14(register_15_q), .in15(register_16_q), .out(R1_D), .sel(R1));
endmodule

module rep_16_32 (
  input  [15:0] entrada,
  output [31:0] saida
);


  assign saida = {{16{1'b0}}, entrada};
endmodule

module rep_20_32 (
  input  [19:0] entrada_20bits,
  output [31:0] saida_32bits
);


  assign saida_32bits = {{12{1'b0}}, entrada_20bits};
endmodule

module rep_28_32 (
  input  [27:0] entra_28bits,
  output [31:0] saida_32bits
);


  assign saida_32bits = {4'b0000, entra_28bits};
endmodule

module ula_to_mem (
  input  [31:0] entrada,
  output [19:0] saida
);


  assign saida = entrada[19:0];
endmodule

module IF___ID (
  input  [31:0] add_4,
  input  [31:0] pc,
  input  CLK,
  input  Clear,
  output [31:0] out_5,
  output [31:0] out_6
);

  Register #(.width(32)) register_1 (.D(add_4), .en(1'b1), .Q(out_5), .clk(CLK), .clr(Clear));
  Register #(.width(32)) register_2 (.D(pc), .en(1'b1), .Q(out_6), .clk(CLK), .clr(Clear));
endmodule

module ID___EX (
  input  data_hazard,
  input  [31:0] in_2,
  input  ResDst,
  input  regwrite,
  input  branch,
  input  MemRead,
  input  MeToReg,
  input  ula_op0,
  input  ula_op1,
  input  MemWrite,
  input  ula_src,
  input  [31:0] reg0,
  input  [31:0] reg1,
  input  [31:0] data_write,
  input  [3:0] in_15,
  input  [3:0] in_16,
  input  CLK,
  input  Clear,
  output data_hazard_2,
  output [31:0] out_20,
  output RegDst,
  output regwrite_2,
  output branch_2,
  output MemRead_2,
  output MemTo_Reg,
  output ula_op0_2,
  output ula_op1_2,
  output MemWrite_2,
  output ula_src_2,
  output [31:0] out_30,
  output [31:0] out_31,
  output [31:0] out_32,
  output [3:0] out_33,
  output [3:0] out_34
);

  Register #(.width(1)) register_1 (.D(data_hazard), .en(1'b1), .Q(data_hazard_2), .clk(CLK), .clr(Clear));
  Register #(.width(32)) register_2 (.D(in_2), .en(1'b1), .Q(out_20), .clk(CLK), .clr(Clear));
  Register #(.width(1)) register_3 (.D(ResDst), .en(1'b1), .Q(RegDst), .clk(CLK), .clr(Clear));
  Register #(.width(1)) register_4 (.D(regwrite), .en(1'b1), .Q(regwrite_2), .clk(CLK), .clr(Clear));
  Register #(.width(1)) register_5 (.D(branch), .en(1'b1), .Q(branch_2), .clk(CLK), .clr(Clear));
  Register #(.width(1)) register_6 (.D(MemRead), .en(1'b1), .Q(MemRead_2), .clk(CLK), .clr(Clear));
  Register #(.width(1)) register_7 (.D(MeToReg), .en(1'b1), .Q(MemTo_Reg), .clk(CLK), .clr(Clear));
  Register #(.width(1)) register_8 (.D(ula_op0), .en(1'b1), .Q(ula_op0_2), .clk(CLK), .clr(Clear));
  Register #(.width(1)) register_9 (.D(ula_op1), .en(1'b1), .Q(ula_op1_2), .clk(CLK), .clr(Clear));
  Register #(.width(1)) register_10 (.D(MemWrite), .en(1'b1), .Q(MemWrite_2), .clk(CLK), .clr(Clear));
  Register #(.width(1)) register_11 (.D(ula_src), .en(1'b1), .Q(ula_src_2), .clk(CLK), .clr(Clear));
  Register #(.width(32)) register_12 (.D(reg0), .en(1'b1), .Q(out_30), .clk(CLK), .clr(Clear));
  Register #(.width(32)) register_13 (.D(reg1), .en(1'b1), .Q(out_31), .clk(CLK), .clr(Clear));
  Register #(.width(32)) register_14 (.D(data_write), .en(1'b1), .Q(out_32), .clk(CLK), .clr(Clear));
  Register #(.width(4)) register_15 (.D(in_15), .en(1'b1), .Q(out_33), .clk(CLK), .clr(Clear));
  Register #(.width(4)) register_16 (.D(in_16), .en(1'b1), .Q(out_34), .clk(CLK), .clr(Clear));
endmodule

module EX___MEM (
  input  [31:0] in_1,
  input  in_2,
  input  in_3,
  input  in_4,
  input  in_5,
  input  in_6,
  input  in_7,
  input  [31:0] in_8,
  input  [31:0] in_9,
  input  [3:0] in_10,
  input  CLK,
  input  CLEAR,
  output [31:0] out_13,
  output out_14,
  output out_15,
  output out_16,
  output out_17,
  output out_18,
  output out_19,
  output [31:0] out_20,
  output [31:0] out_21,
  output [3:0] out_22
);

  Register #(.width(32)) register_1 (.D(in_1), .en(1'b1), .Q(out_13), .clk(CLK), .clr(CLEAR));
  Register #(.width(1)) register_2 (.D(in_2), .en(1'b1), .Q(out_14), .clk(CLK), .clr(CLEAR));
  Register #(.width(1)) register_3 (.D(in_3), .en(1'b1), .Q(out_15), .clk(CLK), .clr(CLEAR));
  Register #(.width(1)) register_4 (.D(in_4), .en(1'b1), .Q(out_16), .clk(CLK), .clr(CLEAR));
  Register #(.width(1)) register_5 (.D(in_5), .en(1'b1), .Q(out_17), .clk(CLK), .clr(CLEAR));
  Register #(.width(1)) register_6 (.D(in_6), .en(1'b1), .Q(out_18), .clk(CLK), .clr(CLEAR));
  Register #(.width(1)) register_7 (.D(in_7), .en(1'b1), .Q(out_19), .clk(CLK), .clr(CLEAR));
  Register #(.width(32)) register_8 (.D(in_8), .en(1'b1), .Q(out_20), .clk(CLK), .clr(CLEAR));
  Register #(.width(32)) register_9 (.D(in_9), .en(1'b1), .Q(out_21), .clk(CLK), .clr(CLEAR));
  Register #(.width(4)) register_10 (.D(in_10), .en(1'b1), .Q(out_22), .clk(CLK), .clr(CLEAR));
endmodule

module MEM___WB (
  input  RegWrite,
  input  MemToReg,
  input  [31:0] in_3,
  input  [31:0] in_4,
  input  [3:0] _24_27,
  input  CLK,
  input  CLEAR,
  output RegWrite_2,
  output MemToReg_2,
  output [31:0] out_10,
  output [31:0] out_11,
  output [3:0] out_12
);

  Register #(.width(1)) register_1 (.D(RegWrite), .en(1'b1), .Q(RegWrite_2), .clk(CLK), .clr(CLEAR));
  Register #(.width(1)) register_2 (.D(MemToReg), .en(1'b1), .Q(MemToReg_2), .clk(CLK), .clr(CLEAR));
  Register #(.width(32)) register_3 (.D(in_3), .en(1'b1), .Q(out_10), .clk(CLK), .clr(CLEAR));
  Register #(.width(32)) register_4 (.D(in_4), .en(1'b1), .Q(out_11), .clk(CLK), .clr(CLEAR));
  Register #(.width(4)) register_5 (.D(_24_27), .en(1'b1), .Q(out_12), .clk(CLK), .clr(CLEAR));
endmodule

module rep_8_32 (
  input  [31:0] in_1,
  output [7:0] out_2
);


  assign out_2 = in_1[7:0];
endmodule

module teste (
  input  [15:0] in_1
);
endmodule
